// Logisim project alu.circ as structural Verilog: 1 circuit, main circuit main
module main (
  input  [31:0] X,
  input  [31:0] Y,
  input  [3:0] Switch,
  output Signed_Overflow,
  output Equal,
  output [31:0] Result
);

  wire addO, addOut, comparator_1_lt, comparator_2_lt, sign, sOut, subO;
  wire [31:0] adder_1_out, addResult, and_out, bit_extender_1_out, bit_extender_2_out, negator_1_out,
       negator_2_out, or_out, shifter_1_out, shifter_2_out, shifter_3_out, subResult, subtractor_2_out,
       xor_out;

  Multiplexer #(.select(4)) multiplexer_1 (
    .in0(1'b0), .in1(1'b0), .in2(1'b0), .in3(addO), .in4(1'b0), .in5(1'b0), .in6(subO), .in7(1'b0),
    .in8(1'b0), .in9(1'b0), .in10(1'b0), .in11(1'b0), .in12(1'b0), .in13(1'b0), .in14(1'b0), .in15(1'b0),
    .out(Signed_Overflow), .sel(Switch));  // open: en
  Negator #(.width(32)) negator_1 (.in(X), .out(negator_1_out));
  Comparator #(.width(32)) comparator_1 (.a(X), .b(Y), .eq(Equal), .lt(comparator_1_lt));  // open: gt
  Negator #(.width(32)) negator_2 (.in(Y), .out(negator_2_out));
  Adder #(.width(32)) adder_1 (.a(X), .b(Y), .out(adder_1_out));  // open: cin, cout
  assign and_out = X & Y;  // AND_Gate and, 32 bits wide
  Comparator #(.width(32)) comparator_2 (.a(negator_1_out), .b(negator_2_out), .lt(comparator_2_lt));  // open: gt, eq
  Shifter #(.width(32)) shifter_1 (.in(X), .\dist (Y[4:0]), .out(shifter_1_out));
  Subtractor #(.width(32)) subtractor_1 (.a(X), .b(Y), .out(subResult), .bout(sOut));  // open: bin
  Subtractor #(.width(32)) subtractor_2 (.a(X), .b(Y), .out(subtractor_2_out));  // open: bin, bout
  assign or_out = X | Y;  // OR_Gate or, 32 bits wide
  Shifter #(.width(32), .shift("lr")) shifter_2 (.in(X), .\dist (Y[4:0]), .out(shifter_2_out));
  assign bit_extender_1_out = {{31{1'b0}}, comparator_1_lt};  // Bit_Extender bit_extender_1
  Shifter #(.width(32), .shift("ar")) shifter_3 (.in(X), .\dist (Y[4:0]), .out(shifter_3_out));
  assign xor_out = X ^ Y;  // XOR_Gate xor, 32 bits wide
  Adder #(.width(32)) adder_2 (.a(X), .b(Y), .out(addResult), .cout(addOut));  // open: cin
  assign bit_extender_2_out = {{31{1'b0}}, comparator_2_lt};  // Bit_Extender bit_extender_2
  Multiplexer #(.select(4), .width(32)) multiplexer_2 (
    .in0(shifter_1_out), .in1(shifter_2_out), .in2(shifter_3_out), .in3(addResult), .in4(adder_1_out),
    .in6(subResult), .in7(subtractor_2_out), .in10(and_out), .in11(or_out), .in12(xor_out),
    .in14(bit_extender_1_out), .in15(bit_extender_2_out), .out(Result), .sel(Switch));  // open: in5, in8, in9, in13, en
  or or_2 (sign, X[31], Y[31]);
  xor xor_2 (subO, sign, subResult[31]);
  xor xor_3 (addO, sign, addResult[31]);

  // Other names for the same wires on the sheet: AoS = Signed_Overflow

  // Notes on the sheet:
  //   INPUTS to your circuit
  //   sltu -y
  //   addu
  //   sltu -x
  //   slt
  //   sltu
  //   sll
  //   sra
  //   DON'T CHANGE THE LOCATIONS OF THE INPUTS AND OUTPUTS!
  //   sub
  //   subu
  //   srl
  //   add
  //   OUTPUTS from your circuit
  //   1st splitter: add result[31]
  //   2nd splitter: x[31]
  //   3rd splitter: y[31]
  //   4th splitter: sub result[31]
endmodule
