// Logisim project cpu.circ as structural Verilog: 3 circuits, main circuit mult
module main (
  input  [31:0] INSTRUCTION,
  input  CLOCK,
  input  [3:0] ALU_OP,
  input  clk,
  input  clk_2,
  output [31:0] FETCH_ADDRESS,
  output [31:0] s0_Value,
  output [31:0] s1_Value,
  output [31:0] s2_Value,
  output [31:0] ra_Value,
  output [31:0] sp_Value
);

  wire ALUSrc, and_3_out, and_4_out, BEQen, BNEen, branch, BRANCHen, comparator_2_eq, comparator_3_eq,
       comparator_4_eq, comparator_12_eq, comparator_14_eq, comparator_15_eq, Equal, I_O_p5, isLUI, JAL, jr,
       jump, Load_StoreEN, LoadWordEN, main_3_p1, main_3_p3, main_3_p8, MemToReg, MemWrite, mf, mfHI, mfLO,
       mult, not_1_out, or_1_out, or_3_out, R_Type, RegDest, RegWrite, ShiftEN, StoreWordEN;
  wire [3:0] ALU_I_op, ALU_R_op, multiplexer_9_out, multiplexer_10_out, multiplexer_11_out,
       multiplexer_16_out, multiplexer_17_out, multiplexer_19_out, multiplexer_20_out, multiplexer_21_out,
       multiplexer_22_out;
  wire [4:0] multiplexer_1_out, WR;
  wire [6:0] random_1_out;
  wire [31:0] _32imm, adder_2_out, bit_extender_1_out, bit_extender_4_out, bit_extender_5_out, HI, HIorLO,
       LO, M, main_2_result, mult_1_hi, mult_1_lo, multiplexer_3_out, multiplexer_5_out, multiplexer_6_out,
       multiplexer_14_out, PC, PC_4, PCBranch, R_rs, R_rt, result, ResultLUI, shamt32, shifter_1_out, WD, Y;

  or or_1 (or_1_out, RegDest, Load_StoreEN);
  Register #(.width(32)) u_PC (.D(PC), .Q(FETCH_ADDRESS), .clk(CLOCK));  // open: en, clr
  assign bit_extender_1_out = {{6{INSTRUCTION[25]}}, INSTRUCTION[25:0]};  // Bit_Extender bit_extender_1
  Multiplexer #(.width(5), .enable("false")) multiplexer_1 (
    .in0(INSTRUCTION[15:11]), .in1(INSTRUCTION[20:16]), .out(multiplexer_1_out), .sel(or_1_out));
  Multiplexer #(.width(5), .enable("false")) multiplexer_2 (
    .in0(multiplexer_1_out), .in1({5{1'b1}}), .out(WR), .sel(JAL));
  Multiplexer #(.width(32), .enable("false")) multiplexer_3 (
    .in0(WD), .in1(M), .out(multiplexer_3_out), .sel(MemToReg));
  Comparator #(.width(6), .mode("unsigned")) comparator_1 (
    .a(INSTRUCTION[31:26]), .b({6{1'b0}}), .eq(R_Type));  // open: gt, lt
  assign _32imm = {{16{INSTRUCTION[15]}}, INSTRUCTION[15:0]};  // Bit_Extender bit_extender_2
  Comparator #(.width(6), .mode("unsigned")) comparator_2 (
    .a(INSTRUCTION[5:0]), .b({6{1'b0}}), .eq(comparator_2_eq));  // open: gt, lt
  Comparator #(.width(6), .mode("unsigned")) comparator_3 (
    .a(INSTRUCTION[5:0]), .b(6'b000010), .eq(comparator_3_eq));  // open: gt, lt
  Comparator #(.width(6), .mode("unsigned")) comparator_4 (
    .a(INSTRUCTION[5:0]), .b(6'b000011), .eq(comparator_4_eq));  // open: gt, lt
  Comparator #(.width(6), .mode("unsigned")) comparator_5 (
    .a(INSTRUCTION[31:26]), .b(6'b000100), .eq(BEQen));  // open: gt, lt
  Comparator #(.width(6), .mode("unsigned")) comparator_6 (
    .a(INSTRUCTION[31:26]), .b(6'b000101), .eq(BNEen));  // open: gt, lt
  Comparator #(.width(6), .mode("unsigned")) comparator_7 (
    .a(INSTRUCTION[31:26]), .b(6'b100011), .eq(LoadWordEN));  // open: gt, lt
  Comparator #(.width(6), .mode("unsigned")) comparator_8 (
    .a(INSTRUCTION[31:26]), .b(6'b101011), .eq(StoreWordEN));  // open: gt, lt
  Adder #(.width(32)) adder_1 (.a(FETCH_ADDRESS), .b(32'h4), .out(PC_4));  // open: cin, cout
  Shifter #(.width(32)) shifter_1 (.in(bit_extender_1_out), .\dist (5'b00010), .out(shifter_1_out));
  Multiplexer #(.width(32), .enable("false")) multiplexer_4 (
    .in0(multiplexer_3_out), .in1(PC_4), .out(result), .sel(JAL));
  or or_2 (mf, mfLO, mfHI);
  Multiplexer #(.width(32), .enable("false")) multiplexer_5 (
    .in0(PC_4), .in1(shifter_1_out), .out(multiplexer_5_out), .sel(jump));
  Comparator #(.width(6)) comparator_9 (.a(INSTRUCTION[5:0]), .b(6'b010000), .eq(mfHI));  // open: gt, lt
  Comparator #(.width(6)) comparator_10 (.a(INSTRUCTION[5:0]), .b(6'b011000), .eq(mult));  // open: gt, lt
  Comparator #(.width(6)) comparator_11 (.a(INSTRUCTION[5:0]), .b(6'b010010), .eq(mfLO));  // open: gt, lt
  Comparator #(.width(6)) comparator_12 (.a(INSTRUCTION[31:26]), .b(6'b000010), .eq(comparator_12_eq));  // open: gt, lt
  Comparator #(.width(6)) comparator_13 (.a(INSTRUCTION[31:26]), .b(6'b000011), .eq(JAL));  // open: gt, lt
  Comparator #(.width(6)) comparator_14 (.a(INSTRUCTION[5:0]), .b(6'b001000), .eq(comparator_14_eq));  // open: gt, lt
  Comparator #(.width(6), .mode("unsigned")) comparator_15 (
    .a(INSTRUCTION[31:26]), .b({6{1'b0}}), .eq(comparator_15_eq));  // open: gt, lt
  or or_3 (or_3_out, comparator_2_eq, comparator_3_eq, comparator_4_eq);
  Multiplexer #(.width(32), .enable("false")) multiplexer_6 (
    .in0(multiplexer_5_out), .in1(R_rs), .out(multiplexer_6_out), .sel(jr));
  Adder #(.width(32)) adder_2 (.a(PCBranch), .b(PC_4), .out(adder_2_out));  // open: cin, cout
  or or_4 (jump, comparator_12_eq, JAL);
  and and_1 (jr, comparator_14_eq, R_Type);
  and and_2 (ShiftEN, comparator_15_eq, or_3_out);
  assign shamt32 = {{27{1'b0}}, INSTRUCTION[10:6]};  // Bit_Extender bit_extender_3
  or or_5 (Load_StoreEN, LoadWordEN, StoreWordEN);
  Multiplexer #(.width(32), .enable("false")) multiplexer_7 (
    .in0(multiplexer_6_out), .in1(adder_2_out), .out(PC), .sel(BRANCHen));
  Multiplexer #(.select(5), .width(32)) multiplexer_8 (
    .in0({32{1'b0}}), .in1({32{1'b0}}), .in2({32{1'b0}}), .in3({32{1'b0}}), .in4({32{1'b0}}),
    .in5({32{1'b0}}), .in6({32{1'b0}}), .in7({32{1'b0}}), .in8({32{1'b0}}), .in9({32{1'b0}}),
    .in10({32{1'b0}}), .in11({32{1'b0}}), .in12({32{1'b0}}), .in13({32{1'b0}}), .in14({32{1'b0}}),
    .in15({32{1'b0}}), .in16(HI), .in17({32{1'b0}}), .in18(LO), .in19({32{1'b0}}), .in20({32{1'b0}}),
    .in21({32{1'b0}}), .in22({32{1'b0}}), .in23({32{1'b0}}), .in24({32{1'b0}}), .in25({32{1'b0}}),
    .in26({32{1'b0}}), .in27({32{1'b0}}), .in28({32{1'b0}}), .in29({32{1'b0}}), .in30({32{1'b0}}),
    .in31({32{1'b0}}), .out(HIorLO), .sel(INSTRUCTION[4:0]));  // open: en
  not not_1 (not_1_out, Equal);
  Multiplexer #(.width(4), .enable("false")) multiplexer_9 (
    .in0(4'b0011), .in1(4'b0100), .out(multiplexer_9_out), .sel(INSTRUCTION[26]));
  Multiplexer #(.width(4), .enable("false")) multiplexer_10 (
    .in0(4'b1110), .in1(4'b1111), .out(multiplexer_10_out), .sel(INSTRUCTION[26]));
  Multiplexer #(.width(4), .enable("false")) multiplexer_11 (
    .in0(4'b1010), .in1(4'b1011), .out(multiplexer_11_out), .sel(INSTRUCTION[26]));
  and and_3 (and_3_out, BEQen, branch, Equal);
  and and_4 (and_4_out, BNEen, branch, not_1_out);
  regfile_main main_1 (
    .Read_Register_1(INSTRUCTION[25:21]), .Read_Register_2(INSTRUCTION[20:16]), .Write_Register(WR),
    .Write_Data(result), .Write_Enable(RegWrite), .Clock(CLOCK), .Read_Data_1(R_rs), .Read_Data_2(R_rt),
    .s0_Value(s0_Value), .s1_Value(s1_Value), .s2_Value(s2_Value), .ra_Value(ra_Value), .sp_Value(sp_Value));
  mult mult_1 (.X(R_rs), .Y(Y), .LO(mult_1_lo), .HI(mult_1_hi));  // open: Clock, Mult
  Multiplexer #(.width(32), .enable("false")) multiplexer_12 (.in0(ResultLUI), .in1(_32imm), .out(Y), .sel(ALUSrc));
  Multiplexer #(.select(5), .width(4)) multiplexer_13 (
    .in0(4'b0000), .in1(4'b0000), .in2(4'b0000), .in3(4'b0000), .in4(multiplexer_9_out),
    .in5(multiplexer_10_out), .in6(multiplexer_11_out), .in7(4'b0000), .in8(4'b0000), .in9(4'b0000),
    .in10(4'b0000), .in11(4'b0000), .in12(4'b0000), .in13(4'b0000), .in14(4'b0000), .in15(4'b0000),
    .in16(4'b0000), .in17(4'b0000), .in18(4'b0000), .in19(4'b0000), .in20(4'b0000), .in21(4'b0000),
    .in22(4'b0000), .in23(4'b0000), .in24(4'b0000), .in25(4'b0000), .in26(4'b0000), .in27(4'b0000),
    .in28(4'b0000), .in29(4'b0000), .in30(4'b0000), .in31(4'b0000), .out(ALU_I_op), .sel(INSTRUCTION[31:27]));  // open: en
  or or_6 (BRANCHen, and_3_out, and_4_out);
  Multiplexer #(.width(32), .enable("false")) multiplexer_14 (
    .in0(R_rs), .in1(shamt32), .out(multiplexer_14_out), .sel(ShiftEN));
  Register #(.width(32)) loReg (.D(mult_1_lo), .clk(clk));  // open: en, Q, clr
  Register #(.width(32)) hiReg (.D(mult_1_hi), .clk(clk_2));  // open: en, Q, clr
  Multiplexer #(.width(32), .enable("false")) multiplexer_15 (
    .in0(R_rt), .in1({INSTRUCTION[15:0], {16{1'b0}}}), .out(ResultLUI), .sel(isLUI));
  assign bit_extender_4_out = {{16{INSTRUCTION[15]}}, INSTRUCTION[15:0]};  // Bit_Extender bit_extender_4
  alu_main main_2 (
    .Switch(multiplexer_16_out), .X(multiplexer_14_out), .Equal(Equal), .Result(main_2_result), .Y(Y));  // open: Signed_Overflow
  Multiplexer #(.width(4), .enable("false")) multiplexer_16 (
    .in0(ALU_I_op), .in1(ALU_R_op), .out(multiplexer_16_out), .sel(R_Type));
  Multiplexer #(.width(4), .enable("false")) multiplexer_17 (
    .in0(4'b0110), .in1(4'b0111), .out(multiplexer_17_out), .sel(INSTRUCTION[0]));
  // I_O I_O: pin names not known; wires that end beside it: bit_extender_4_out, CLOCK, MemWrite, R_rt, I_O_p5
  Multiplexer #(.width(32), .enable("false")) multiplexer_18 (.in0(main_2_result), .in1(HIorLO), .out(WD), .sel(mf));
  Multiplexer #(.width(4), .enable("false")) multiplexer_19 (
    .in0(4'b0001), .in1(4'b0010), .out(multiplexer_19_out), .sel(INSTRUCTION[0]));
  Multiplexer #(.width(4), .enable("false")) multiplexer_20 (
    .in0(4'b0011), .in1(4'b0100), .out(multiplexer_20_out), .sel(INSTRUCTION[0]));
  Multiplexer #(.width(4), .enable("false")) multiplexer_21 (
    .in0(4'b1010), .in1(4'b1011), .out(multiplexer_21_out), .sel(INSTRUCTION[0]));
  Multiplexer #(.width(4), .enable("false")) multiplexer_22 (
    .in0(4'b1110), .in1(4'b1111), .out(multiplexer_22_out), .sel(INSTRUCTION[0]));
  assign bit_extender_5_out = {{16{INSTRUCTION[15]}}, INSTRUCTION[15:0]};  // Bit_Extender bit_extender_5
  Shifter #(.width(32)) shifter_2 (.in(_32imm), .\dist (5'b00010), .out(PCBranch));
  Random #(.width(7)) random_1 (.clk(I_O_p5), .out(random_1_out));  // open: next, clr
  mult Mult_2 (.X(R_rs), .Y(Y), .Clock(CLOCK), .Mult(mult), .LO(LO), .HI(HI));
  // Probe on ALU_R_op
  Multiplexer #(.select(5), .width(4)) multiplexer_23 (
    .in0(4'b0000), .in1(multiplexer_19_out), .in2(4'b0000), .in3(4'b0000), .in4(4'b0000), .in5(4'b0000),
    .in6(4'b0000), .in7(4'b0000), .in8(4'b0000), .in9(4'b0000), .in10(4'b0000), .in11(4'b0000),
    .in12(4'b0000), .in13(4'b0000), .in14(4'b0000), .in15(4'b0000), .in16(multiplexer_20_out),
    .in17(multiplexer_17_out), .in18(multiplexer_21_out), .in19(4'b1100), .in20(4'b0000),
    .in21(multiplexer_22_out), .in22(4'b0000), .in23(4'b0000), .in24(4'b0000), .in25(4'b0000),
    .in26(4'b0000), .in27(4'b0000), .in28(4'b0000), .in29(4'b0000), .in30(4'b0000), .in31(4'b0000),
    .out(ALU_R_op), .sel(INSTRUCTION[5:1]));  // open: en
  // mem_main main_3: pin names not known; wires that end beside it: main_3_p1, main_3_p1, main_3_p3, main_3_p3, bit_extender_5_out, R_rt, MemWrite, main_3_p8, CLOCK, M
  TTY tty_1 (.data(random_1_out), .clk(CLOCK));  // open: we, clr
  Control control_1 (
    .a(INSTRUCTION[31]), .b(INSTRUCTION[30]), .c(INSTRUCTION[29]), .d(INSTRUCTION[28]), .e(INSTRUCTION[27]),
    .f(INSTRUCTION[26]), .RegWrite(RegWrite), .RegDest(RegDest), .MemToReg(MemToReg), .ALUSrc(ALUSrc),
    .MemWrite(MemWrite), .Branch(branch), .isLUI(isLUI));

  // Other names for the same wires on the sheet: address[25:0] = INSTRUCTION[25:0]; funct[5:0] = INSTRUCTION[5:0];
  //   imm[15:0] = INSTRUCTION[15:0]; jAddress[25:0] = INSTRUCTION[25:0]; shamt[4:0] = INSTRUCTION[10:6];
  //   rd[4:0] = INSTRUCTION[15:11]; clk_t = CLOCK; fetch_addr[31:0] = FETCH_ADDRESS; rt[4:0] = INSTRUCTION[20:16];
  //   rs[4:0] = INSTRUCTION[25:21]; op[5:0] = INSTRUCTION[31:26]; ra[31:0] = ra_Value; s0[31:0] = s0_Value;
  //   s1[31:0] = s1_Value; s2[31:0] = s2_Value; sp[31:0] = sp_Value

  // Notes on the sheet:
  //   Output
  //   These are outputs/inputs from run.circ
  //   Inputs
  //   These are DEBUG/TEST outputs from your circuit.
endmodule

module mult (
  input  [31:0] X,
  input  [31:0] Y,
  input  Clock,
  input  Mult,
  output [31:0] LO,
  output [31:0] HI
);

  wire [31:0] multiplier_1_cout, multiplier_1_out;

  Multiplier #(.width(32)) multiplier_1 (.a(X), .b(Y), .out(multiplier_1_out), .cout(multiplier_1_cout));  // open: cin
  Register #(.width(32)) u_LO (.D(multiplier_1_out), .en(Mult), .Q(LO), .clk(Clock));  // open: clr
  Register #(.width(32)) u_HI (.D(multiplier_1_cout), .en(Mult), .Q(HI), .clk(Clock));  // open: clr
endmodule

module Control (
  input  a,
  input  b,
  input  c,
  input  d,
  input  e,
  input  f,
  output RegWrite,
  output RegDest,
  output MemToReg,
  output ALUSrc,
  output MemWrite,
  output Branch,
  output isLUI
);

  wire and_1_out, and_2_out, and_3_out, and_4_out, and_5_out, and_6_out, and_7_out, and_8_out, and_9_out,
       and_10_out, and_11_out, and_12_out, and_13_out, and_14_out, and_15_out, and_16_out, and_17_out,
       and_18_out, and_19_out, and_20_out, and_21_out, and_22_out, and_23_out, and_24_out, and_25_out,
       and_26_out, and_27_out, and_28_out, and_29_out, and_30_out, and_31_out, and_32_out, and_33_out,
       not_1_out, not_2_out, not_3_out, not_4_out, not_5_out, not_6_out, not_7_out, not_8_out, not_9_out,
       not_10_out, not_11_out, not_12_out, not_13_out, not_14_out, not_15_out, not_16_out, not_17_out,
       not_18_out, not_19_out, not_20_out, not_21_out, not_22_out, not_23_out, not_24_out, not_25_out,
       not_26_out, not_27_out, not_28_out, not_29_out, not_30_out, not_31_out, not_32_out, not_33_out,
       not_34_out, not_35_out, not_36_out, not_37_out, not_38_out, not_39_out, not_40_out, not_41_out,
       not_42_out, not_43_out, not_44_out, not_45_out, not_46_out, not_47_out;

  not not_1 (not_1_out, e);
  not not_2 (not_2_out, f);
  not not_3 (not_3_out, b);
  not not_4 (not_4_out, c);
  not not_5 (not_5_out, b);
  not not_6 (not_6_out, a);
  not not_7 (not_7_out, d);
  not not_8 (not_8_out, e);
  not not_9 (not_9_out, f);
  not not_10 (not_10_out, c);
  not not_11 (not_11_out, e);
  not not_12 (not_12_out, f);
  not not_13 (not_13_out, a);
  not not_14 (not_14_out, b);
  not not_15 (not_15_out, d);
  not not_16 (not_16_out, a);
  not not_17 (not_17_out, b);
  not not_18 (not_18_out, e);
  not not_19 (not_19_out, a);
  not not_20 (not_20_out, b);
  not not_21 (not_21_out, c);
  not not_22 (not_22_out, c);
  not not_23 (not_23_out, c);
  not not_24 (not_24_out, f);
  not not_25 (not_25_out, a);
  not not_26 (not_26_out, b);
  not not_27 (not_27_out, d);
  not not_28 (not_28_out, a);
  not not_29 (not_29_out, b);
  not not_30 (not_30_out, e);
  not not_31 (not_31_out, b);
  not not_32 (not_32_out, d);
  not not_33 (not_33_out, a);
  not not_34 (not_34_out, c);
  not not_35 (not_35_out, c);
  not not_36 (not_36_out, b);
  not not_37 (not_37_out, d);
  not not_38 (not_38_out, c);
  not not_39 (not_39_out, e);
  not not_40 (not_40_out, f);
  not not_41 (not_41_out, d);
  not not_42 (not_42_out, f);
  not not_43 (not_43_out, c);
  not not_44 (not_44_out, e);
  not not_45 (not_45_out, f);
  not not_46 (not_46_out, a);
  not not_47 (not_47_out, b);
  and and_1 (and_1_out, not_1_out, not_2_out);
  and and_2 (and_2_out, not_3_out, not_4_out, e, f);
  and and_3 (and_3_out, not_5_out, d);
  and and_4 (and_4_out, not_6_out, c);
  and and_5 (and_5_out, b, not_7_out);
  and and_6 (and_6_out, b, not_8_out);
  and and_7 (and_7_out, b, not_9_out);
  and and_8 (and_8_out, a, not_10_out);
  and and_9 (and_9_out, a, not_11_out);
  and and_10 (and_10_out, a, not_12_out);
  and and_11 (and_11_out, a, d);
  and and_12 (and_12_out, not_13_out, not_14_out, c, not_15_out);
  and and_13 (and_13_out, not_16_out, not_17_out, c, not_18_out);
  and and_14 (and_14_out, not_19_out, not_20_out, c, f);
  and and_15 (and_15_out, not_21_out, f);
  and and_16 (and_16_out, not_22_out, e);
  and and_17 (and_17_out, not_23_out, d);
  and and_18 (and_18_out, d, e, not_24_out);
  and and_19 (and_19_out, not_25_out, not_26_out, c, not_27_out);
  and and_20 (and_20_out, not_28_out, not_29_out, c, not_30_out);
  and and_21 (and_21_out, not_31_out, c, not_32_out, e, f);
  and and_22 (and_22_out, not_33_out, b, not_34_out, d, e, f);
  and and_23 (and_23_out, b, not_35_out, d, e, f);
  and and_24 (and_24_out, a, not_36_out, c, not_37_out);
  and and_25 (and_25_out, not_38_out, d, not_39_out);
  and and_26 (and_26_out, c, d, e, not_40_out);
  and and_27 (and_27_out, b, not_41_out);
  and and_28 (and_28_out, b, not_42_out);
  and and_29 (and_29_out, b, c);
  and and_30 (and_30_out, a, not_43_out);
  and and_31 (and_31_out, a, not_44_out);
  and and_32 (and_32_out, a, not_45_out);
  and and_33 (and_33_out, a, d);
  and and_34 (isLUI, not_46_out, not_47_out, c, d, e, f);
  or or_1 (RegWrite, and_1_out, and_2_out, and_3_out, and_4_out, and_5_out, and_6_out, and_7_out, and_8_out, and_9_out, and_10_out, and_11_out);
  or or_2 (RegDest, and_12_out, and_13_out, and_14_out);
  or or_3 (MemToReg, and_15_out, and_16_out, and_17_out, and_18_out, b, a);
  or or_4 (ALUSrc, and_19_out, and_20_out, and_21_out, and_22_out);
  or or_5 (MemWrite, and_23_out, and_24_out);
  or or_6 (Branch, and_25_out, and_26_out, and_27_out, and_28_out, and_29_out, and_30_out, and_31_out, and_32_out, and_33_out);
endmodule
