// Logisim project regfile.circ as structural Verilog: 1 circuit, main circuit main
module main (
  input  [4:0] Read_Register_1,
  input  [4:0] Read_Register_2,
  input  [4:0] Write_Register,
  input  [31:0] Write_Data,
  input  Write_Enable,
  input  Clock,
  output [31:0] s0_Value,
  output [31:0] s1_Value,
  output [31:0] s2_Value,
  output [31:0] ra_Value,
  output [31:0] sp_Value,
  output [31:0] Read_Data_1,
  output [31:0] Read_Data_2
);

  wire [31:0] Input0, Input1, Input2, Input3, Input4, Input5, Input6, Input7, Input8, Input9, Input10,
       Input11, Input12, Input13, Input14, Input15, Input16, Input17, Input18, Input19, Input20, Input21,
       Input22, Input23, Input24, Input25, Input26, Input27, Input28, Input29, Input30, Input31, Read0,
       Read1, Read2, Read3, Read4, Read5, Read6, Read7, Read8, Read9, Read10, Read11, Read12, Read13, Read14,
       Read15, Read19, Read20, Read21, Read22, Read23, Read24, Read25, Read26, Read27, Read28, Read30;

  Demultiplexer #(.select(5), .width(32)) demultiplexer_1 (
    .out0(Input0), .out1(Input1), .out2(Input2), .out3(Input3), .out4(Input4), .out5(Input5), .out6(Input6),
    .out7(Input7), .out8(Input8), .out9(Input9), .out10(Input10), .out11(Input11), .out12(Input12),
    .out13(Input13), .out14(Input14), .out15(Input15), .out16(Input16), .out17(Input17), .out18(Input18),
    .out19(Input19), .out20(Input20), .out21(Input21), .out22(Input22), .out23(Input23), .out24(Input24),
    .out25(Input25), .out26(Input26), .out27(Input27), .out28(Input28), .out29(Input29), .out30(Input30),
    .out31(Input31), .in(Write_Data), .sel(Write_Register), .en(Write_Enable));
  Multiplexer #(.select(5), .width(32)) multiplexer_1 (
    .in0(Read0), .in1(Read1), .in2(Read2), .in3(Read3), .in4(Read4), .in5(Read5), .in6(Read6), .in7(Read7),
    .in8(Read8), .in9(Read9), .in10(Read10), .in11(Read11), .in12(Read12), .in13(Read13), .in14(Read14),
    .in15(Read15), .in16(s0_Value), .in17(s1_Value), .in18(s2_Value), .in19(Read19), .in20(Read20),
    .in21(Read21), .in22(Read22), .in23(Read23), .in24(Read24), .in25(Read25), .in26(Read26), .in27(Read27),
    .in28(Read28), .in29(sp_Value), .in30(Read30), .in31(ra_Value), .out(Read_Data_1), .sel(Read_Register_1));  // open: en
  Multiplexer #(.select(5), .width(32)) multiplexer_2 (
    .in0(Read0), .in1(Read1), .in2(Read2), .in3(Read3), .in4(Read4), .in5(Read5), .in6(Read6), .in7(Read7),
    .in8(Read8), .in9(Read9), .in10(Read10), .in11(Read11), .in12(Read12), .in13(Read13), .in14(Read14),
    .in15(Read15), .in16(s0_Value), .in17(s1_Value), .in18(s2_Value), .in19(Read19), .in20(Read20),
    .in21(Read21), .in22(Read22), .in23(Read23), .in24(Read24), .in25(Read25), .in26(Read26), .in27(Read27),
    .in28(Read28), .in29(sp_Value), .in30(Read30), .in31(ra_Value), .out(Read_Data_2), .sel(Read_Register_2));  // open: en
  Register #(.width(32)) zero (.D(Input0), .Q(Read0), .clk(Clock));  // open: en, clr
  Register #(.width(32)) at (.D(Input1), .Q(Read1), .clk(Clock));  // open: en, clr
  Register #(.width(32)) v0 (.D(Input2), .Q(Read2), .clk(Clock));  // open: en, clr
  Register #(.width(32)) v1 (.D(Input3), .Q(Read3), .clk(Clock));  // open: en, clr
  Register #(.width(32)) a0 (.D(Input4), .Q(Read4), .clk(Clock));  // open: en, clr
  Register #(.width(32)) a1 (.D(Input5), .Q(Read5), .clk(Clock));  // open: en, clr
  Register #(.width(32)) a2 (.D(Input6), .Q(Read6), .clk(Clock));  // open: en, clr
  Register #(.width(32)) a3 (.D(Input7), .Q(Read7), .clk(Clock));  // open: en, clr
  Register #(.width(32)) t0 (.D(Input8), .Q(Read8), .clk(Clock));  // open: en, clr
  Register #(.width(32)) t1 (.D(Input9), .Q(Read9), .clk(Clock));  // open: en, clr
  Register #(.width(32)) t2 (.D(Input10), .Q(Read10), .clk(Clock));  // open: en, clr
  Register #(.width(32)) t3 (.D(Input11), .Q(Read11), .clk(Clock));  // open: en, clr
  Register #(.width(32)) t4 (.D(Input12), .Q(Read12), .clk(Clock));  // open: en, clr
  Register #(.width(32)) t5 (.D(Input13), .Q(Read13), .clk(Clock));  // open: en, clr
  Register #(.width(32)) t6 (.D(Input14), .Q(Read14), .clk(Clock));  // open: en, clr
  Register #(.width(32)) t7 (.D(Input15), .Q(Read15), .clk(Clock));  // open: en, clr
  Register #(.width(32)) s0 (.D(Input16), .Q(s0_Value), .clk(Clock));  // open: en, clr
  Register #(.width(32)) s1 (.D(Input17), .Q(s1_Value), .clk(Clock));  // open: en, clr
  Register #(.width(32)) s2 (.D(Input18), .Q(s2_Value), .clk(Clock));  // open: en, clr
  Register #(.width(32)) s3 (.D(Input19), .Q(Read19), .clk(Clock));  // open: en, clr
  Register #(.width(32)) s4 (.D(Input20), .Q(Read20), .clk(Clock));  // open: en, clr
  Register #(.width(32)) s5 (.D(Input21), .Q(Read21), .clk(Clock));  // open: en, clr
  Register #(.width(32)) s6 (.D(Input22), .Q(Read22), .clk(Clock));  // open: en, clr
  Register #(.width(32)) s7 (.D(Input23), .Q(Read23), .clk(Clock));  // open: en, clr
  Register #(.width(32)) t8 (.D(Input24), .Q(Read24), .clk(Clock));  // open: en, clr
  Register #(.width(32)) t9 (.D(Input25), .Q(Read25), .clk(Clock));  // open: en, clr
  Register #(.width(32)) k0 (.D(Input26), .Q(Read26), .clk(Clock));  // open: en, clr
  Register #(.width(32)) k1 (.D(Input27), .Q(Read27), .clk(Clock));  // open: en, clr
  Register #(.width(32)) gp (.D(Input28), .Q(Read28), .clk(Clock));  // open: en, clr
  Register #(.width(32)) sp (.D(Input29), .Q(sp_Value), .clk(Clock));  // open: en, clr
  Register #(.width(32)) fp (.D(Input30), .Q(Read30), .clk(Clock));  // open: en, clr
  Register #(.width(32)) ra (.D(Input31), .Q(ra_Value), .clk(Clock));  // open: en, clr

  // Other names for the same wires on the sheet: clk = Clock; Read16[31:0] = s0_Value; Read17[31:0] = s1_Value;
  //   Read18[31:0] = s2_Value; Read29[31:0] = sp_Value; Read31[31:0] = ra_Value; read_data1[31:0] = Read_Data_1;
  //   read_data2[31:0] = Read_Data_2; read_reg1[4:0] = Read_Register_1; read_reg2[4:0] = Read_Register_2;
  //   write_en = Write_Enable; write_reg[4:0] = Write_Register

  // Notes on the sheet:
  //   INPUTS to your circuit
  //   DON'T CHANGE THE LOCATIONS OF THE INPUTS AND OUTPUTS!
  //   These are DEBUG/TEST outputs from your circuit.
  //   OUTPUTS from your circuit
endmodule
