// Logisim project func_test.circ as structural Verilog: 1 circuit, main circuit main
module main (
  output [31:0] s0_Value,
  output [31:0] s1_Value,
  output [31:0] s2_Value,
  output [31:0] sp_Value,
  output halt
);

  wire clock_1_out;
  wire [31:0] counter_1_q, fetch_addr, Instruction, main_1_ra_value;

  Clock clock_1 (.out(clock_1_out));
  cpu_main main_1 (
    .INSTRUCTION(Instruction), .CLOCK(clock_1_out), .FETCH_ADDRESS(fetch_addr), .s0_Value(s0_Value),
    .s1_Value(s1_Value), .s2_Value(s2_Value), .ra_Value(main_1_ra_value), .sp_Value(sp_Value));  // open: ALU_OP, clk_2, clk
  Counter #(.width(32), .max('hffffffff)) counter_1 (
    .Q(counter_1_q), .clk(clock_1_out));  // open: load, D, count, carry, clr
  Comparator #(.width(32)) comparator_1 (.a(counter_1_q), .b(32'hc), .eq(halt));  // open: gt, lt
  // Probe on fetch_addr
  ROM #(.addrWidth(24), .dataWidth(32)) rom_1 (.addr(fetch_addr[25:2]), .data(Instruction));  // open: sel
  // Probe on Instruction

  // Notes on the sheet:
  //   YOUR CPU SHOULD FIT IN HERE!
  //   Instruction Memory
  //   contents of rom_1 (hex, n*v repeats v):
  //   341d0000 2008000c 1002020 c000006 404020 800000a 844820 1244820 91020 3e00008 35100000 37f10000
endmodule
